# Fritzing sketch 01-Promicro-L298-HC05 (saved by Fritzing 0.9.4)
breadboards: 1

parts:
  M1 = DC Motor
  Componente2 = Bluetooth HC-05 Macho
  Pro_Micro1 = Pro Micro
  L298N1 = L298N DC motor driver
  M2 = DC Motor
  R3 = Resistor [tolerance=±5% resistance=10k package=THT]
  R4 = Resistor [tolerance=±1% resistance=20k package=THT]

nets:
  N1: M1.pin_1, L298N1.OUT2
  N2: M1.pin_2, L298N1.OUT1
  N3: Componente2.TXD, Pro_Micro1.RX0
  N4: Componente2.RXD, R3.Pin_1, R4.Pin_1
  VCC: Componente2.VCC, Pro_Micro1.RAW, L298N1.12V, L298N1.5V
  N5: Componente2.GND, Pro_Micro1.GND#23
  N6: Pro_Micro1.TX1, R3.Pin_0
  N7: Pro_Micro1.GND#3, R4.Pin_0
  N8: Pro_Micro1.GND#4, L298N1.GND
  N9: Pro_Micro1.D5, L298N1.IN4
  N10: Pro_Micro1.D6, L298N1.IN3
  N11: Pro_Micro1.D7, L298N1.ENB
  N12: Pro_Micro1.D8, L298N1.ENA
  N13: Pro_Micro1.D9, L298N1.IN2
  N14: Pro_Micro1.D10, L298N1.IN1
  N15: L298N1.OUT3, M2.pin_1
  N16: L298N1.OUT4, M2.pin_2

notes:
  Retire o jumper 5VEN (Enable internal 5v), que fica próximo aos Bornes OUT1 e OUT2)

custom parts:
  Pro Micro: The SparkFun Pro Micro is a complete USB-based microcontoller development system, in a very small footprint, capable of implementing many types of projects. All programming can be done via the USB port.
  L298N DC motor driver: 2x DC motor driver with 78M05 positive voltage regulator (7..35 V) L298N: max 46 V, 2 A Set 5 V Enable jumper to enable 5 V regultor (needed for the L298N) and +5 V output at screw terminal or supply external +5 V at screw terminal Set ENA and/or ENB to +5 V to enable motor permanently or supply ENA and/or ENB with PWM signal IN1 and IN2 set rotation directory for motor A (OUT1/OUT2) IN2 and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
